# Fritzing sketch Blinky (saved by Fritzing 0.7.11b)
breadboards: 1

parts:
  S1 = Pushbutton [package="[THT]"]
  Netduino1 = Netduino Plus
  LED1 = green smd LED [package="0805 [SMD]"]
  R2 = Resistor [tolerance=±5% resistance=1k package=THT]

nets:
  N1: S1.Pin_1, S1.Pin_2, Netduino1.D1_TX0
  N2: S1.Pin_3, S1.Pin_4, Netduino1.GND, LED1.cathode
  N3: Netduino1.D0_RX0, R2.Pin_1
  N4: LED1.anode, R2.Pin_0
