# Fritzing sketch Potentiometer (saved by Fritzing 0.7.11b)
breadboards: 1

parts:
  Netduino1 = Netduino Plus
  R1 = Trimmer Potentiometer [maximum_resistance=10kΩ package=THT]

nets:
  N1: Netduino1.GND, R1.leg2
  N2: Netduino1.3V3, R1.leg1
  N3: Netduino1.A0, R1.wiper
